# Fritzing sketch ElbanquosKitchentimer_MK1 (saved by Fritzing 0.9.3b)
breadboards: 2

parts:
  S1 = Pushbutton [package="[THT]"]  # not connected
  S2 = Pushbutton [package="[THT]"]  # not connected
  S3 = Pushbutton [package="[THT]"]  # not connected
  S4 = Pushbutton [package="[THT]"]  # not connected
  LED1 = smd LED [color="Red (633nm)" package="1206 [SMD]"]  # not connected
  LED2 = smd LED [color="Red (633nm)" package="1206 [SMD]"]  # not connected
  LED3 = smd LED [color="Red (633nm)" package="1206 [SMD]"]  # not connected
  LED4 = smd LED [color="Red (633nm)" package="1206 [SMD]"]  # not connected
  TM1638_-_Led_Button_Module = IC, DIP package, 10 pins [chip_label=IC]
  RE1 = Rotary Encoder [package=THT]
  Rotary_Button_Function = Pushbutton [package="[THT]"]
  J1 = Piezo Speaker
  R1 = Resistor [tolerance=±5% resistance=560 package=THT]
  7_Segment1 = 7 Segment Display  # not connected
  7_Segment2 = 7 Segment Display  # not connected
  7_Segment3 = 7 Segment Display  # not connected
  7_Segment4 = 7 Segment Display  # not connected
  7_Segment5 = 7 Segment Display  # not connected
  7_Segment6 = 7 Segment Display  # not connected
  7_Segment7 = 7 Segment Display  # not connected
  7_Segment8 = 7 Segment Display  # not connected
  R3 = Resistor [tolerance=±5% resistance=4.7k package=THT]
  Power_Adapter = Power plug
  The_Nano = Arduino Nano (Rev3.0)
  R2 = Trimmer Potentiometer [maximum_resistance=100kΩ package=THT]
  Q1 = NPN-Transistor [package="TO92 [THT]"]
  J2 = Camdenboss CTB0158-4 [part_number=CTB0158-4 package=THT]
  C1 = Ceramic Capacitor [capacitance=100nF package="100 mil [THT, multilayer]"]

nets:
  N1: TM1638_-_Led_Button_Module.pin1, The_Nano.5V
  GND: TM1638_-_Led_Button_Module.pin2, RE1.EncoderPinC, Rotary_Button_Function.Pin_3, Rotary_Button_Function.Pin_4, J1.pin1, R1.Pin_1, R3.Pin_1, Power_Adapter.GND, The_Nano.GND, J2.pin2, C1.1
  N2: TM1638_-_Led_Button_Module.pin3, The_Nano.D2
  N3: TM1638_-_Led_Button_Module.pin4, The_Nano.D3
  N4: TM1638_-_Led_Button_Module.pin5, The_Nano.D4
  N5: RE1.EncoderPinA, The_Nano.D11/MOSI
  N6: RE1.EncoderPinB, The_Nano.D10
  N7: Rotary_Button_Function.Pin_1, Rotary_Button_Function.Pin_2, The_Nano.D12/MISO
  N8: J1.pin2, R3.Pin_0, Q1.E
  N9: R1.Pin_0, R2.leg1
  VCC: Power_Adapter.VCC, The_Nano.VIN, Q1.C, J2.pin3, J2.pin4, C1.0
  N10: The_Nano.D5, R2.leg2
  N11: R2.wiper, Q1.B

notes:
  Led & Keyboard With
  TM1638
  Some Magic here->
