# Fritzing sketch ElbanquosKitchentimer_MK2 (saved by Fritzing 0.9.10b)
circuit board: 2.02544cm x 2.4722cm
circuit board: 9.60653cm x 1.86029cm
circuit board: 12.1005cm x 7.93745cm
circuit board: 9.27391cm x 1.58578cm
breadboards: 5

parts:
  S2 = Pushbutton [package="[THT]"]
  S4 = Pushbutton [package="[THT]"]
  S3 = Pushbutton [package="[THT]"]
  S1 = Pushbutton [package="[THT]"]
  RE1 = Rotary Encoder [package=THT]
  Rotary_Button_Function = Pushbutton [package="[THT]"]
  R5 = Resistor [tolerance=±5% resistance=560 power=0.25 package=THT]
  Power_Adapter = Power plug
  The_Nano = Arduino Nano (Rev3.0)
  POT1 = Trimmer Potentiometer [maximum_resistance=10kΩ knob_status=50% power=0.5W package=THT]
  button_led_shift_reg = 74HC595 [package="DIP16 [THT]"]
  R4 = Resistor [tolerance=±10% resistance=220 power=0.25 package=THT]
  R3 = Resistor [tolerance=±10% resistance=220 power=0.25 package=THT]
  R2 = Resistor [tolerance=±10% resistance=220 power=0.25 package=THT]
  R1 = Resistor [tolerance=±10% resistance=220 power=0.25 package=THT]
  LED3r = LED - 3mm [color="Red (633nm)" current=0.030 package="3 mm [THT]"]
  LED2r = LED - 3mm [color="Red (633nm)" current=0.030 package="3 mm [THT]"]
  LED1r = LED - 3mm [color="Red (633nm)" current=0.030 package="3 mm [THT]"]
  J1 = rounded female pin header, 5 pins [form="♀ (female rounded)"]
  J4 = rounded female pin header, 3 pins [form="♀ (female rounded)"]
  J3 = rounded female pin header, 3 pins [form="♀ (female rounded)"]
  J2 = rounded female pin header, 3 pins [form="♀ (female rounded)"]
  J5 = female pin header, 5 pins [form="♀ (female)"]
  LED4r = LED - 3mm [color="Red (633nm)" current=0.030 package="3 mm [THT]"]
  J5m = male pin header, 5 pins [form="♂ (male)"]
  J4m = male pin header, 3 pins [form="♂ (male)"]
  j2m = male pin header, 3 pins [form="♂ (male)"]
  j3m = male pin header, 3 pins [form="♂ (male)"]
  J1m = male pin header, 5 pins [form="♂ (male)"]
  R13 = Resistor [tolerance=±5% resistance=22k power=0.25 package=THT]
  R12 = Resistor [tolerance=±5% resistance=22k power=0.25 package=THT]
  R11 = Resistor [tolerance=±5% resistance=22k power=0.25 package=THT]
  R14 = Resistor [tolerance=±5% resistance=22k power=0.25 package=THT]
  LED2g = smd LED [color="Green (555nm)" package="1206 [SMD]"]
  LED1g = smd LED [color="Green (555nm)" package="1206 [SMD]"]
  LED3g = smd LED [color="Green (555nm)" package="1206 [SMD]"]
  LED4g = smd LED [color="Green (555nm)" package="1206 [SMD]"]
  7_Segment8 = 7 Segment Display
  7_Segment7 = 7 Segment Display
  7_Segment6 = 7 Segment Display
  7_Segment5 = 7 Segment Display
  7_Segment4 = 7 Segment Display
  7_Segment3 = 7 Segment Display
  7_Segment2 = 7 Segment Display
  7_Segment1 = 7 Segment Display
  LED_Controller(MAX7_) = MAX7219 [package=dil24]
  R15 = Resistor [tolerance=±5% resistance=10k power=0.25 package=THT]
  R16 = Resistor [tolerance=±5% resistance=10k power=0.25 package=THT]
  J6 = rounded female pin header, 4 pins [form="♀ (female rounded)"]
  SPK = Piezo Speaker
  R17 = Resistor [tolerance=±5% resistance=4.7k power=0.25 package=THT]
  Q1 = NPN-Transistor [package="TO92 [THT]"]

nets:
  N1: S2.Pin_1, S2.Pin_2, The_Nano.A2, J2.pin1, j2m.pin1, R12.Pin_1
  VCC: S2.Pin_3, S2.Pin_4, S4.Pin_1, S4.Pin_2, S3.Pin_3, S3.Pin_4, S1.Pin_3, S1.Pin_4, The_Nano.5V, button_led_shift_reg.MR, button_led_shift_reg.VCC, J1.pin5, J5.pin1, J5m.pin1, J1m.pin5, LED_Controller(MAX7_).VCC, R15.Pin_0, R16.Pin_0
  N2: S4.Pin_3, S4.Pin_4, The_Nano.A4, J4.pin1, J4m.pin1, R14.Pin_1
  N3: S3.Pin_1, S3.Pin_2, The_Nano.A3, J3.pin1, j3m.pin1, R13.Pin_1
  N4: S1.Pin_1, S1.Pin_2, The_Nano.A5, J1.pin2, J1m.pin2, R11.Pin_1
  N5: RE1.EncoderPinA, The_Nano.D3, R15.Pin_1, J6.pin2
  GND: RE1.EncoderPinC, Rotary_Button_Function.Pin_1, Rotary_Button_Function.Pin_2, R5.Pin_1, Power_Adapter.GND, The_Nano.GND, button_led_shift_reg.GND, button_led_shift_reg.OE, J1.pin1, J5.pin2, J5m.pin2, J1m.pin1, R13.Pin_0, R12.Pin_0, R11.Pin_0, R14.Pin_0, LED_Controller(MAX7_).GND, J6.pin3, SPK.pin1, R17.Pin_1
  N6: RE1.EncoderPinB, The_Nano.D2, R16.Pin_1, J6.pin4
  N7: Rotary_Button_Function.Pin_3, Rotary_Button_Function.Pin_4, The_Nano.D4, J6.pin1
  N8: R5.Pin_0, POT1.leg1
  VCC_2: Power_Adapter.VCC, The_Nano.VIN, Q1.C
  N9: The_Nano.D5, POT1.leg2
  N10: The_Nano.D6, button_led_shift_reg.SH_CP
  N11: The_Nano.D7, button_led_shift_reg.ST_CP
  N12: The_Nano.D8, button_led_shift_reg.DS
  N13: The_Nano.D10, J5.pin5, J5m.pin5, LED_Controller(MAX7_).CLK
  N14: The_Nano.D11/MOSI, J5.pin4, J5m.pin4, LED_Controller(MAX7_).LOAD
  N15: The_Nano.D12/MISO, J5.pin3, J5m.pin3, LED_Controller(MAX7_).DIN
  N16: POT1.wiper, Q1.B
  N17: button_led_shift_reg.Q1, R1.Pin_1
  N18: button_led_shift_reg.Q2, LED2r.cathode, J2.pin3, j2m.pin3, LED2g.anode
  N19: button_led_shift_reg.Q3, R2.Pin_1
  N20: button_led_shift_reg.Q4, LED3r.cathode, J3.pin3, j3m.pin3, LED3g.anode
  N21: button_led_shift_reg.Q5, R3.Pin_1
  N22: button_led_shift_reg.Q6, J4.pin3, LED4r.cathode, J4m.pin3, LED4g.anode
  N23: button_led_shift_reg.Q7, R4.Pin_1
  N24: button_led_shift_reg.Q0, LED1r.cathode, J1.pin4, J1m.pin4, LED1g.anode
  N25: R4.Pin_0, J4.pin2, LED4r.anode, J4m.pin2, LED4g.cathode
  N26: R3.Pin_0, LED3r.anode, J3.pin2, j3m.pin2, LED3g.cathode
  N27: R2.Pin_0, LED2r.anode, J2.pin2, j2m.pin2, LED2g.cathode
  N28: R1.Pin_0, LED1r.anode, J1.pin3, J1m.pin3, LED1g.cathode
  N29: 7_Segment8.Segment_G, 7_Segment8.Segment_F, 7_Segment8.common_anode, 7_Segment8.Segment_E, 7_Segment8.Segment_D, 7_Segment8.Segment_DP, 7_Segment8.Segment_C, 7_Segment8.Segment_B, 7_Segment8.Segment_A
  N30: 7_Segment7.Segment_G, 7_Segment7.Segment_F, 7_Segment7.common_anode, 7_Segment7.Segment_E, 7_Segment7.Segment_D, 7_Segment7.Segment_DP, 7_Segment7.Segment_C, 7_Segment7.Segment_B, 7_Segment7.Segment_A
  N31: 7_Segment6.Segment_G, 7_Segment6.Segment_F, 7_Segment6.common_anode, 7_Segment6.Segment_E, 7_Segment6.Segment_D, 7_Segment6.Segment_DP, 7_Segment6.Segment_C, 7_Segment6.Segment_B, 7_Segment6.Segment_A
  N32: 7_Segment5.Segment_G, 7_Segment5.Segment_F, 7_Segment5.common_anode, 7_Segment5.Segment_E, 7_Segment5.Segment_D, 7_Segment5.Segment_DP, 7_Segment5.Segment_C, 7_Segment5.Segment_B, 7_Segment5.Segment_A
  N33: 7_Segment4.Segment_G, 7_Segment4.Segment_F, 7_Segment4.common_anode, 7_Segment4.Segment_E, 7_Segment4.Segment_D, 7_Segment4.Segment_DP, 7_Segment4.Segment_C, 7_Segment4.Segment_B, 7_Segment4.Segment_A
  N34: 7_Segment3.Segment_G, 7_Segment3.Segment_F, 7_Segment3.common_anode, 7_Segment3.Segment_E, 7_Segment3.Segment_D, 7_Segment3.Segment_DP, 7_Segment3.Segment_C, 7_Segment3.Segment_B, 7_Segment3.Segment_A
  N35: 7_Segment2.Segment_G, 7_Segment2.Segment_F, 7_Segment2.common_anode, 7_Segment2.Segment_E, 7_Segment2.Segment_D, 7_Segment2.Segment_DP, 7_Segment2.Segment_C, 7_Segment2.Segment_B, 7_Segment2.Segment_A
  N36: 7_Segment1.Segment_G, 7_Segment1.Segment_F, 7_Segment1.common_anode, 7_Segment1.Segment_E, 7_Segment1.Segment_D, 7_Segment1.Segment_DP, 7_Segment1.Segment_C, 7_Segment1.Segment_B, 7_Segment1.Segment_A
  N37: SPK.pin2, R17.Pin_0, Q1.E

notes:
  Demo layout for experimental board:
  lower= open wires / Solder bridges
  upper= isolated wires(may cross)
  air=Cables or jumper connects
